// Logisim project Arithmetic_and_Logic_unit.circ as structural Verilog: 1 circuit, main circuit main
module main (
  input  Mode,
  input  [3:0] Operation,
  input  [7:0] Ain,
  input  [7:0] Bin,
  input  Cin,
  output [7:0] Result
);

  wire undriven_11;
  wire [3:0] bitadder_1_out;
  wire [7:0] adder_1_out, and_1_out, buffer_1_out, buffer_2_out, divider_1_out, divider_1_rem,
       multiplexer_1_out, multiplexer_3_out, multiplier_1_out, nand_1_out, negator_1_out, nor_1_out,
       not_1_out, not_2_out, or_1_out, shifter_1_out, shifter_2_out, shifter_3_out, shifter_4_out,
       shifter_5_out, subtractor_1_out, undriven, undriven_2, undriven_3, undriven_4, undriven_5, undriven_6,
       undriven_7, undriven_8, undriven_9, undriven_10, xnor_1_out, xor_1_out;

  // NoConnect on Bin[7]
  // NoConnect on Bin[6]
  // NoConnect on Bin[5]
  // NoConnect on Bin[4]
  // NoConnect on Bin[3]
  assign buffer_1_out = Ain;  // Buffer buffer_1, 8 bits wide
  assign buffer_2_out = Bin;  // Buffer buffer_2, 8 bits wide
  Adder adder_1 (.a(Ain), .b(Bin), .out(adder_1_out), .cin(Cin));  // open: cout
  Subtractor subtractor_1 (.a(Ain), .b(Bin), .out(subtractor_1_out), .bin(Cin));  // open: bout
  Multiplier multiplier_1 (.a(Ain), .b(Bin), .out(multiplier_1_out));  // open: cin, cout
  Divider divider_1 (.a(Ain), .b(Bin), .out(divider_1_out), .rem(divider_1_rem));  // open: upper
  Negator negator_1 (.in(Ain), .out(negator_1_out));
  Shifter shifter_1 (.in(Ain), .\dist (Bin[2:0]), .out(shifter_1_out));
  Shifter #(.shift("lr")) shifter_2 (.in(Ain), .\dist (Bin[2:0]), .out(shifter_2_out));
  Shifter #(.shift("ar")) shifter_3 (.in(Ain), .\dist (Bin[2:0]), .out(shifter_3_out));
  Shifter #(.shift("rl")) shifter_4 (.in(Ain), .\dist (Bin[2:0]), .out(shifter_4_out));
  Shifter #(.shift("rr")) shifter_5 (.in(Ain), .\dist (Bin[2:0]), .out(shifter_5_out));
  BitAdder bitadder_1 (.in0(Ain), .out(bitadder_1_out));
  assign not_1_out = ~Ain;  // NOT_Gate not_1, 8 bits wide
  assign not_2_out = ~Bin;  // NOT_Gate not_2, 8 bits wide
  assign and_1_out = Ain & Bin;  // AND_Gate and_1, 8 bits wide
  assign nand_1_out = ~(Ain & Bin);  // NAND_Gate nand_1, 8 bits wide
  assign or_1_out = Ain | Bin;  // OR_Gate or_1, 8 bits wide
  assign nor_1_out = ~(Ain | Bin);  // NOR_Gate nor_1, 8 bits wide
  assign xor_1_out = Ain ^ Bin;  // XOR_Gate xor_1, 8 bits wide
  assign xnor_1_out = ~(Ain ^ Bin);  // XNOR_Gate xnor_1, 8 bits wide
  Comparator comparator_1 (.a(Ain), .b(Bin));  // open: gt, eq, lt
  // NoConnect on undriven
  // NoConnect on undriven_2
  // NoConnect on undriven_3
  // NoConnect on undriven_4
  // NoConnect on undriven_5
  // NoConnect on undriven_6
  // NoConnect on undriven_7
  // NoConnect on undriven_8
  // NoConnect on undriven_9
  // NoConnect on undriven_10
  // NoConnect on undriven_11
  Multiplexer #(.select(4), .width(8)) multiplexer_1 (
    .in0(adder_1_out), .in1(subtractor_1_out), .in2(multiplier_1_out), .in3(divider_1_out),
    .in4(divider_1_rem), .in5(negator_1_out), .in6(shifter_3_out), .in7({4'b0000, bitadder_1_out}),
    .in8(buffer_1_out), .in9(buffer_2_out), .in10(undriven), .in11(undriven_2), .in12(undriven_3),
    .in13(undriven_4), .in14(undriven_5), .in15(undriven_6), .out(multiplexer_1_out), .sel(Operation));
  Multiplexer #(.width(8)) multiplexer_2 (.in0(multiplexer_1_out), .in1(multiplexer_3_out), .out(Result), .sel(Mode));
  Multiplexer #(.select(4), .width(8)) multiplexer_3 (
    .in0(shifter_1_out), .in1(shifter_2_out), .in2(shifter_4_out), .in3(shifter_5_out), .in4(not_1_out),
    .in5(not_2_out), .in6(and_1_out), .in7(nand_1_out), .in8(or_1_out), .in9(nor_1_out), .in10(xor_1_out),
    .in11(xnor_1_out), .in12(undriven_7), .in13(undriven_8), .in14(undriven_9), .in15(undriven_10),
    .out(multiplexer_3_out), .sel(Operation));
endmodule
