// Logisim project pipeline.circ as structural Verilog
module FetchUnit (
  input  [7:0] instrORimm,
  input  clk,
  input  reset,
  input  delayIN,
  input  stall,
  output [1:0] count,
  output [7:0] pipelineRegisters,
  output [7:0] pipeline,
  output delayOUT,
  output ready,
  output incPC,
  output [7:0] fetchReg
);

  wire and_1_out, nor_1_out, or_1_out, register_1_q;
  wire [7:0] multiplexer_1_out;

  Multiplexer #(.width(8)) multiplexer_1 (.in0({8{1'b0}}), .in1(instrORimm), .out(multiplexer_1_out), .sel(1'b1));
  // Probe on instrORimm
  // NoConnect on multiplexer_1_out[0]
  // NoConnect on multiplexer_1_out[1]
  // NoConnect on multiplexer_1_out[2]
  // NoConnect on multiplexer_1_out[3]
  // NoConnect on multiplexer_1_out[4]
  // NoConnect on multiplexer_1_out[5]
  Register #(.width(1)) register_1 (.D(nor_1_out), .en(1'b1), .clk(clk), .Q(register_1_q), .clr(reset));
  Register register_2 (.D(instrORimm), .en(1'b1), .clk(clk), .Q(fetchReg), .clr(reset));
  or or_1 (or_1_out, multiplexer_1_out[6], multiplexer_1_out[7]);
  and and_1 (and_1_out, or_1_out, nor_1_out);
  nor nor_1 (nor_1_out, count[0], count[1]);
  Counter #(.max('h3), .ongoal("stay"), .width(2)) counter_1 (
    .load(and_1_out), .D(multiplexer_1_out[7:6]), .count(1'b1), .Q(count), .up(1'b0), .clk(clk), .clr(reset));  // open: carry
  Demultiplexer #(.width(8)) demultiplexer_1 (
    .out0(pipelineRegisters), .out1(pipeline), .in(fetchReg), .sel(register_1_q));
  and and_2 (ready, register_1_q, 1'b1);

  assign delayOUT = 1'b1;
  assign incPC = 1'b1;

  // Notes on the sheet:
  //   Note: Ready signal is not meant for enabling the write input, it is to say all the
  //   immediate values are loaded into the pipeline registers to the decode units
  //   currently it is being used for write enable and must be changed in the future
endmodule

module delay (
  input  dIN,
  input  clock,
  input  reset,
  output dOUT,
  output ss
);

  wire d_ff_1_qn, d_ff_2_qn, undriven, undriven_2;

  D_Flip_Flop d_ff_1 (.D(dIN), .clk(clock), .Q(ss), .Qn(d_ff_1_qn), .preset(undriven), .reset(reset));
  // NoConnect on undriven
  D_Flip_Flop d_ff_2 (.D(ss), .clk(clock), .Q(dOUT), .Qn(d_ff_2_qn), .preset(undriven_2), .reset(reset));
  // NoConnect on d_ff_1_qn
  // NoConnect on undriven_2
  // NoConnect on d_ff_2_qn
endmodule

module test2 (
  input  load,
  input  [15:0] FFFFin,
  input  rst
);

  wire clk_out, decodeunit_1_alumode, decodeunit_1_cin, decodeunit_1_dload, decodeunit_1_dstore,
       decodeunit_1_enalu, decodeunit_1_regatodbus, fetchunit_1_delayout, fetchunit_1_incpc,
       fetchunit_1_ready;
  wire [1:0] fetchunit_1_count;
  wire [3:0] decodeunit_1_operation, decodeunit_1_rega, decodeunit_1_regb, decodeunit_1_regres;
  wire [7:0] alu_1_flags, alu_1_result, dataMemory_dout, decodeunit_1_databus, fetchunit_1_fetchreg,
       fetchunit_1_pipeline, fetchunit_1_pipelineregisters, generalpurposeregisters_1_a,
       generalpurposeregisters_1_b, instructionMemory_data, register_1_q, register_2_q, register_3_q,
       register_4_q;
  wire [15:0] decodeunit_1_dataaddr, programcounter_1_ffffout;

  ROM #(.addrWidth(16)) instructionMemory (.addr(programcounter_1_ffffout), .data(instructionMemory_data));
  ProgramCounter programcounter_1 (
    .FFFFin(FFFFin), .enable(fetchunit_1_incpc), .load(load), .clock(clk_out), .reset(rst),
    .FFFFout(programcounter_1_ffffout));
  // Probe on instructionMemory_data
  // Probe on fetchunit_1_fetchreg
  // Probe on fetchunit_1_count
  FetchUnit fetchunit_1 (
    .instrORimm(instructionMemory_data), .clk(clk_out), .reset(rst), .count(fetchunit_1_count),
    .pipelineRegisters(fetchunit_1_pipelineregisters), .pipeline(fetchunit_1_pipeline),
    .delayOUT(fetchunit_1_delayout), .ready(fetchunit_1_ready), .incPC(fetchunit_1_incpc),
    .fetchReg(fetchunit_1_fetchreg));  // open: delayIN, stall
  Register register_1 (
    .D(fetchunit_1_pipelineregisters), .en(fetchunit_1_delayout), .clk(clk_out), .Q(register_1_q), .clr(rst));
  Register register_2 (.D(register_1_q), .en(fetchunit_1_delayout), .clk(clk_out), .Q(register_2_q), .clr(rst));
  Register register_3 (.D(register_2_q), .en(fetchunit_1_delayout), .clk(clk_out), .Q(register_3_q), .clr(rst));
  decodeUnit decodeunit_1 (
    .pipelineReg1(register_1_q), .pipelineReg2(register_2_q), .pipelineReg3(register_3_q),
    .pipelineIn(fetchunit_1_pipeline), .readyIN(fetchunit_1_ready), .clk(clk_out), .rst(rst),
    .databus(decodeunit_1_databus), .dataaddr(decodeunit_1_dataaddr), .enALU(decodeunit_1_enalu),
    .regAtoDBus(decodeunit_1_regatodbus), .operation(decodeunit_1_operation), .regA(decodeunit_1_rega),
    .regB(decodeunit_1_regb), .regRes(decodeunit_1_regres), .ALUmode(decodeunit_1_alumode),
    .Cin(decodeunit_1_cin), .dload(decodeunit_1_dload), .dstore(decodeunit_1_dstore));  // open: instraddr, pipelineOut, readyOUT
  RAM #(.addrWidth(16), .asyncread("true"), .\type ("nonvolatile")) dataMemory (
    .addr(decodeunit_1_dataaddr), .we(decodeunit_1_dstore), .oe(decodeunit_1_dload), .clk(clk_out),
    .din(decodeunit_1_databus), .dout(dataMemory_dout));
  Pull_Resistor pull_resistor_1 (.node(decodeunit_1_dataaddr));
  // Probe on decodeunit_1_rega
  // NoConnect on decodeunit_1_rega[3]
  // NoConnect on decodeunit_1_regb[3]
  // NoConnect on decodeunit_1_regres[3]
  // Probe on decodeunit_1_regb
  // Probe on decodeunit_1_regres
  assign decodeunit_1_databus = decodeunit_1_dload ? dataMemory_dout : 8'bz;  // Controlled_Buffer controlled_buffer_1
  Clock clk (.out(clk_out));
  assign decodeunit_1_databus = decodeunit_1_regatodbus ? generalpurposeregisters_1_a : 8'bz;  // Controlled_Buffer controlled_buffer_2
  GeneralPurposeRegisters generalpurposeregisters_1 (
    .write_Addr(decodeunit_1_regres[2:0]), .A_addr(decodeunit_1_rega[2:0]), .reset(rst), .clock(clk_out),
    .B_addr(decodeunit_1_regb[2:0]), .data(decodeunit_1_databus), .A(generalpurposeregisters_1_a),
    .B(generalpurposeregisters_1_b));
  // Probe on decodeunit_1_operation
  assign decodeunit_1_databus = decodeunit_1_enalu ? alu_1_result : 8'bz;  // Controlled_Buffer controlled_buffer_3
  // Probe on alu_1_result
  Register register_4 (.D(alu_1_flags), .en(decodeunit_1_enalu), .clk(clk_out), .Q(register_4_q), .clr(rst));
  ALU alu_1 (
    .Mode(decodeunit_1_alumode), .Operation(decodeunit_1_operation), .Ain(generalpurposeregisters_1_a),
    .Bin(generalpurposeregisters_1_b), .Cin(decodeunit_1_cin), .Result(alu_1_result), .Flags(alu_1_flags));
  // Probe on register_4_q

  // Notes on the sheet:
  //   contents of instructionMemory (hex, n*v repeats v):
  //   de 0 0 1 de 1 0 2 e0 8 0 1 e0 9 0 2 82 21 1 e0 8 0 1
  //   PIPELINE REGISTERS 
  //   DATA BUS 
endmodule

module test1 (
  input  [7:0] instrORimm,
  input  clk,
  input  reset,
  input  delayIn,
  input  insertNOPE,
  output [7:0] PipelineRegisters,
  output [7:0] nextStage,
  output ready,
  output incPC
);

  wire and_1_out, and_2_out, c, or_1_out, or_2_out, register_1_q, t_ff_1_q, t_ff_1_qn;
  wire [1:0] counter_1_q;
  wire [7:0] demultiplexer_1_out0, demultiplexer_1_out1, multiplexer_1_out, register_2_q, register_3_q,
       register_4_q, register_5_q, register_6_q;

  Multiplexer #(.width(8)) multiplexer_1 (.in0({8{1'b0}}), .in1(instrORimm), .out(multiplexer_1_out), .sel(delayIn));
  // NoConnect on multiplexer_1_out[0]
  // NoConnect on multiplexer_1_out[1]
  // NoConnect on multiplexer_1_out[2]
  // NoConnect on multiplexer_1_out[3]
  // NoConnect on multiplexer_1_out[4]
  // NoConnect on multiplexer_1_out[5]
  Register #(.width(1)) register_1 (.D(c), .en(delayIn), .clk(clk), .Q(register_1_q), .clr(reset));
  or or_1 (or_1_out, delayIn, c);
  // NOT_Gate not_1 has open pins: in=insertNOPE, out=open
  or or_2 (or_2_out, multiplexer_1_out[6], multiplexer_1_out[7]);
  and and_1 (and_1_out, or_2_out, c);
  nor nor_1 (c, counter_1_q[0], counter_1_q[1]);
  Register register_2 (.D(instrORimm), .en(delayIn), .clk(clk), .Q(register_2_q), .clr(reset));
  // NOT_Gate not_2 has open pins: in=t_ff_1_q, out=open
  T_Flip_Flop t_ff_1 (.T(or_1_out), .clk(clk), .Q(t_ff_1_q), .Qn(t_ff_1_qn), .reset(reset), .preset(1'b0));
  // NoConnect on t_ff_1_qn
  Counter #(.max('h3), .ongoal("stay"), .width(2)) counter_1 (
    .load(and_1_out), .D(multiplexer_1_out[7:6]), .count(delayIn), .Q(counter_1_q), .up(1'b0), .clk(clk),
    .clr(reset));  // open: carry
  Demultiplexer #(.width(8)) demultiplexer_1 (
    .out0(demultiplexer_1_out0), .out1(demultiplexer_1_out1), .in(register_2_q), .sel(register_1_q));
  and and_2 (and_2_out, register_1_q, delayIn);
  Register register_3 (.D(demultiplexer_1_out0), .en(delayIn), .clk(clk), .Q(register_3_q), .clr(reset));
  Register register_4 (.D(demultiplexer_1_out1), .en(and_2_out), .clk(clk), .Q(register_4_q), .clr(reset));
  Register register_5 (.D(register_3_q), .en(delayIn), .clk(clk), .Q(register_5_q), .clr(reset));
  Register register_6 (.D(register_4_q), .en(and_2_out), .clk(clk), .Q(register_6_q), .clr(reset));
  Register register_7 (.D(register_5_q), .en(delayIn), .clk(clk), .Q(PipelineRegisters), .clr(reset));
  Register register_8 (.D(register_6_q), .en(and_2_out), .clk(clk), .Q(nextStage), .clr(reset));

  // Notes on the sheet:
  //   delay is used for requesting the pipeline to halt the next cycle 
  //   and it is not meant for handling pipeline hazards
endmodule

module decodeUnit (
  input  [7:0] pipelineReg1,
  input  [7:0] pipelineReg2,
  input  [7:0] pipelineReg3,
  input  [7:0] pipelineIn,
  input  readyIN,
  input  clk,
  input  rst,
  output [7:0] databus,
  output [15:0] instraddr,
  output [15:0] dataaddr,
  output enALU,
  output regAtoDBus,
  output [3:0] operation,
  output [3:0] regA,
  output [3:0] regB,
  output [3:0] regRes,
  output [7:0] pipelineOut,
  output readyOUT,
  output ALUmode,
  output Cin,
  output dload,
  output dstore
);

  wire [2:0] rom_1_data;
  wire [15:0] rom_2_data;
  wire [15:3] rom_1_data_2;
  wire [15:4] multiplexer_1_out;

  Register register_1 (.D(pipelineIn), .en(readyIN), .clk(clk), .Q(pipelineOut), .clr(rst));
  // NoConnect on pipelineOut[7]
  // NoConnect on pipelineOut[6]
  ROM #(.addrWidth(6), .dataWidth(16)) rom_1 (.addr(pipelineOut[5:0]), .data({rom_1_data_2, rom_1_data}));
  ROM #(.addrWidth(6), .dataWidth(16)) rom_2 (.addr(pipelineOut[5:0]), .data(rom_2_data));
  // NoConnect on rom_1_data_2[3]
  // NoConnect on rom_1_data_2[4]
  // NoConnect on rom_1_data_2[5]
  // NoConnect on rom_1_data_2[6]
  // NoConnect on rom_1_data_2[7]
  // NoConnect on rom_1_data_2[8]
  // NoConnect on rom_1_data_2[9]
  // NoConnect on rom_1_data_2[10]
  // NoConnect on rom_1_data_2[11]
  // NoConnect on rom_1_data_2[12]
  // NoConnect on rom_1_data_2[13]
  // NoConnect on rom_1_data_2[14]
  // NoConnect on rom_1_data_2[15]
  Multiplexer #(.width(16)) multiplexer_1 (
    .in0({16{1'b0}}), .in1(rom_2_data), .out({multiplexer_1_out, dstore, dload, Cin, ALUmode}), .sel(readyIN));
  // NoConnect on multiplexer_1_out[4]
  // NoConnect on multiplexer_1_out[5]
  // NoConnect on multiplexer_1_out[6]
  // NoConnect on multiplexer_1_out[7]
  // NoConnect on multiplexer_1_out[8]
  // NoConnect on multiplexer_1_out[9]
  // NoConnect on multiplexer_1_out[10]
  // NoConnect on multiplexer_1_out[11]
  // NoConnect on multiplexer_1_out[12]
  // NoConnect on multiplexer_1_out[13]
  // NoConnect on multiplexer_1_out[14]
  // NoConnect on multiplexer_1_out[15]
  pipelineRegFormatSelector pipelineregformatselector_1 (
    .pipelineReg1(pipelineReg1), .pipelineReg2(pipelineReg2), .pipelineReg3(pipelineReg3),
    .modeselect(rom_1_data), .ready(readyIN), .dataBus(databus), .instrAddrBus(instraddr),
    .dataAddrBus(dataaddr), .enALU(enALU), .enRegAtoDBus(regAtoDBus), .operation(operation), .regA(regA),
    .regB(regB), .regRes(regRes));

  assign readyOUT = readyIN;

  // Notes on the sheet:
  //   contents of rom_1 (hex, n*v repeats v):
  //   29*0 4 4 0 8
  //   contents of rom_2 (hex, n*v repeats v):
  //   29*0 3 1 0 2
  //   Note: implement Ready signal it is not just a write enable signal it must only decode and execute instruction when on
endmodule

module pipelineRegFormatSelector (
  input  [7:0] pipelineReg1,
  input  [7:0] pipelineReg2,
  input  [7:0] pipelineReg3,
  input  [2:0] modeselect,
  input  ready,
  output [7:0] dataBus,
  output [15:0] instrAddrBus,
  output [15:0] dataAddrBus,
  output enALU,
  output enRegAtoDBus,
  output [3:0] operation,
  output [3:0] regA,
  output [3:0] regB,
  output [3:0] regRes
);

  wire decoder_1_out1, decoder_1_out2, decoder_1_out3, decoder_1_out4, decoder_1_out5, decoder_1_out6,
       decoder_1_out7, pull_resistor_1_node;

  // NoConnect on dataBus
  // NoConnect on instrAddrBus
  // NoConnect on dataAddrBus
  Decoder #(.select(3)) decoder_1 (
    .out0(enALU), .out1(decoder_1_out1), .out2(decoder_1_out2), .out3(decoder_1_out3), .out4(decoder_1_out4),
    .out5(decoder_1_out5), .out6(decoder_1_out6), .out7(decoder_1_out7), .sel(modeselect), .en(ready));
  // NoConnect on pipelineReg3
  // NoConnect on pipelineReg2
  // NoConnect on pipelineReg1[7:4]
  assign dataAddrBus = decoder_1_out1 ? {pipelineReg2, pipelineReg3} : 16'bz;  // Controlled_Buffer controlled_buffer_1
  // NoConnect on pipelineReg1[7:4]
  assign dataAddrBus = decoder_1_out2 ? {pipelineReg2, pipelineReg3} : 16'bz;  // Controlled_Buffer controlled_buffer_2
  // NoConnect on pipelineReg1
  // NoConnect on decoder_1_out4
  // NoConnect on decoder_1_out5
  // NoConnect on decoder_1_out6
  // NoConnect on decoder_1_out7
  assign regRes = enALU ? pipelineReg1[3:0] : 4'bz;  // Controlled_Buffer controlled_buffer_3
  assign operation = enALU ? pipelineReg1[7:4] : 4'bz;  // Controlled_Buffer controlled_buffer_4
  assign regA = enALU ? pipelineReg2[3:0] : 4'bz;  // Controlled_Buffer controlled_buffer_5
  assign regB = enALU ? pipelineReg2[7:4] : 4'bz;  // Controlled_Buffer controlled_buffer_6
  assign regRes = decoder_1_out1 ? pipelineReg1[3:0] : 4'bz;  // Controlled_Buffer controlled_buffer_7
  assign regA = decoder_1_out2 ? pipelineReg1[3:0] : 4'bz;  // Controlled_Buffer controlled_buffer_8
  assign regA = decoder_1_out3 ? pipelineReg1[3:0] : 4'bz;  // Controlled_Buffer controlled_buffer_9
  assign regRes = decoder_1_out3 ? pipelineReg1[7:4] : 4'bz;  // Controlled_Buffer controlled_buffer_10
  // NoConnect on regRes
  // NoConnect on regB
  // NoConnect on regRes
  // NoConnect on regB
  // NoConnect on regA
  // NoConnect on operation
  // NoConnect on regA
  // NoConnect on operation
  Pull_Resistor pull_resistor_1 (.node(pull_resistor_1_node));
  or or_1 (enRegAtoDBus, decoder_1_out3, decoder_1_out2, pull_resistor_1_node, pull_resistor_1_node, pull_resistor_1_node);

  // Notes on the sheet:
  //   load
  //   store
  //   move
  //   ALU operations 
endmodule
